// Logisim project lab1.circ as structural Verilog: 1 circuit, main circuit main
module main (
  input  [3:0] in_1,
  input  [3:0] in_2,
  input  Clock,
  input  [2:0] in_4,
  output [3:0] out_5
);

  wire adder_1_cout, adder_1_out, adder_2_cout, adder_2_out, adder_3_cout, adder_3_out, adder_4_cout,
       adder_4_out, and_1_out, and_2_out, and_3_out, and_4_out, nand_1_out, nand_2_out, nand_3_out,
       nand_4_out, nor_1_out, nor_2_out, nor_3_out, nor_4_out, not_1_out, not_2_out, not_3_out, not_4_out,
       or_1_out, or_2_out, or_3_out, or_4_out, subtractor_1_bout, subtractor_1_out, subtractor_2_bout,
       subtractor_2_out, subtractor_3_bout, subtractor_3_out, subtractor_4_bout, subtractor_4_out, xor_1_out,
       xor_2_out, xor_3_out, xor_4_out;
  wire [3:0] multiplexer_1_out, register_1_q, register_2_q;

  Register #(.width(4)) register_1 (.D(in_1), .Q(register_1_q), .clk(Clock));  // open: en, clr
  Register #(.width(4)) register_2 (.D(in_2), .Q(register_2_q), .clk(Clock));  // open: en, clr
  Adder #(.width(1)) adder_1 (
    .a(register_1_q[0]), .b(register_2_q[0]), .out(adder_1_out), .cout(adder_1_cout));  // open: cin
  not not_1 (not_1_out, register_2_q[0]);
  Subtractor #(.width(1)) subtractor_1 (
    .a(register_1_q[0]), .b(register_2_q[0]), .out(subtractor_1_out), .bout(subtractor_1_bout));  // open: bin
  and and_1 (and_1_out, register_1_q[0], register_2_q[0]);
  or or_1 (or_1_out, register_1_q[0], register_2_q[0]);
  xor xor_1 (xor_1_out, register_1_q[0], register_2_q[0]);
  nand nand_1 (nand_1_out, register_1_q[0], register_2_q[0]);
  nor nor_1 (nor_1_out, register_1_q[0], register_2_q[0]);
  and and_2 (and_2_out, register_1_q[1], register_2_q[1]);
  or or_2 (or_2_out, register_1_q[1], register_2_q[1]);
  xor xor_2 (xor_2_out, register_1_q[1], register_2_q[1]);
  Adder #(.width(1)) adder_2 (
    .a(register_1_q[1]), .b(register_2_q[1]), .out(adder_2_out), .cin(adder_1_cout), .cout(adder_2_cout));
  not not_2 (not_2_out, register_2_q[1]);
  nand nand_2 (nand_2_out, register_1_q[1], register_2_q[1]);
  nor nor_2 (nor_2_out, register_1_q[1], register_2_q[1]);
  Subtractor #(.width(1)) subtractor_2 (
    .a(register_1_q[1]), .b(register_2_q[1]), .out(subtractor_2_out), .bin(subtractor_1_bout),
    .bout(subtractor_2_bout));
  and and_3 (and_3_out, register_1_q[2], register_2_q[2]);
  or or_3 (or_3_out, register_1_q[2], register_2_q[2]);
  xor xor_3 (xor_3_out, register_1_q[2], register_2_q[2]);
  Adder #(.width(1)) adder_3 (
    .a(register_1_q[2]), .b(register_2_q[2]), .out(adder_3_out), .cin(adder_2_cout), .cout(adder_3_cout));
  not not_3 (not_3_out, register_2_q[2]);
  nand nand_3 (nand_3_out, register_1_q[2], register_2_q[2]);
  nor nor_3 (nor_3_out, register_1_q[2], register_2_q[2]);
  Subtractor #(.width(1)) subtractor_3 (
    .a(register_1_q[2]), .b(register_2_q[2]), .out(subtractor_3_out), .bin(subtractor_2_bout),
    .bout(subtractor_3_bout));
  and and_4 (and_4_out, register_1_q[3], register_2_q[3]);
  or or_4 (or_4_out, register_1_q[3], register_2_q[3]);
  xor xor_4 (xor_4_out, register_1_q[3], register_2_q[3]);
  Adder #(.width(1)) adder_4 (
    .a(register_1_q[3]), .b(register_2_q[3]), .out(adder_4_out), .cin(adder_3_cout), .cout(adder_4_cout));
  not not_4 (not_4_out, register_2_q[3]);
  nand nand_4 (nand_4_out, register_1_q[3], register_2_q[3]);
  nor nor_4 (nor_4_out, register_1_q[3], register_2_q[3]);
  Subtractor #(.width(1)) subtractor_4 (
    .a(register_1_q[3]), .b(register_2_q[3]), .out(subtractor_4_out), .bin(subtractor_3_bout),
    .bout(subtractor_4_bout));
  Multiplexer #(.select(3)) multiplexer_1 (
    .in0(and_1_out), .in1(or_1_out), .in2(xor_1_out), .in3(adder_1_out), .in4(not_1_out), .in5(nand_1_out),
    .in6(nor_1_out), .in7(subtractor_1_out), .out(multiplexer_1_out[0]), .sel(in_4));  // open: en
  Multiplexer #(.select(3)) multiplexer_2 (
    .in0(and_2_out), .in1(or_2_out), .in2(xor_2_out), .in3(adder_2_out), .in4(not_2_out), .in5(nand_2_out),
    .in6(nor_2_out), .in7(subtractor_2_out), .out(multiplexer_1_out[1]), .sel(in_4));  // open: en
  Multiplexer #(.select(3)) multiplexer_3 (
    .in0(and_3_out), .in1(or_3_out), .in2(xor_3_out), .in3(adder_3_out), .in4(not_3_out), .in5(nand_3_out),
    .in6(nor_3_out), .in7(subtractor_3_out), .out(multiplexer_1_out[2]), .sel(in_4));  // open: en
  Multiplexer #(.select(3)) multiplexer_4 (
    .in0(and_4_out), .in1(or_4_out), .in2(xor_4_out), .in3(adder_4_out), .in4(not_4_out), .in5(nand_4_out),
    .in6(nor_4_out), .in7(subtractor_4_out), .out(multiplexer_1_out[3]), .sel(in_4));  // open: en
  Register #(.width(4)) register_3 (.D(multiplexer_1_out), .Q(out_5), .clk(Clock));  // open: en, clr

  // Notes on the sheet:
  //   Reg A
  //   Reg B
  //   Opcode
  //   Reg S
endmodule
